# Fritzing sketch layout (saved by Fritzing 0.8.5b)
breadboards: 1

parts:
  Part1 = Arduino Nano (Rev3.0) (ICSP)
  GY1 = MPU-6050 Board GY-521 [form="♀ (female)" package=THT]
  J1 = Piezo Speaker
  BAT1 = BC9VPC [package=bc9vpc]
  Part2 = Bluetooth HC-05 Macho

nets:
  GND: Part1.GND, GY1.pin2, BAT1.V+, Part2.GND
  N1: Part1.D4, Part2.RXD
  N2: Part1.D5, Part2.TXD
  N3: Part1.VIN, BAT1.V-
  5V: Part1.5V, GY1.pin1, J1.pin2, Part2.VCC
  N4: Part1.A5, GY1.pin3
  N5: Part1.A4, GY1.pin4
  N6: Part1.A3, J1.pin1

notes:
  Exterior

custom parts:
  MPU-6050 Board GY-521: Acelerometro y Giroscopio MPU-6050 Board GY-521
